# Fritzing sketch circuit_diagram (saved by Fritzing 0.9.3b)
circuit board: 8.46667cm x 5.64444cm
breadboards: 1

parts:
  Part1 = Arduino Nano (Rev3.0)
  J1 = Piezo Speaker
  U1 = TMP36 [package=to-92]
  Part2 = Adafruit DS3231 [part_number="Adafruit #3013"]

nets:
  N1: Part1.RESET, Part2.!RTC_RST
  GND: Part1.GND, J1.pin1, U1.GND, Part2.GND
  N2: Part1.D2, J1.pin2
  5V: Part1.5V, U1.VCC, Part2.Vin
  N3: Part1.A5, Part2.SCL
  N4: Part1.A4, Part2.SDA
  N5: Part1.A1, U1.VOUT

custom parts:
  Adafruit DS3231: The datasheet for the DS3231 explains that this part is an "Extremely Accurate I²C-Integrated RTC/TCXO/Crystal". And, hey, it does exactly what it says on the tin! This Real Time Clock (RTC) is the most precise you can get in a small, low power package. Most RTCs use an external 32kHz timing crystal that is used to keep time with low current draw. And that's all well and good, but those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
